// Logisim project aiAlu.circ as structural Verilog
module Half_Adder (
  input  a,
  input  b,
  output S,
  output C
);

  xor xor_1 (S, b, a);
  and and_1 (C, b, a);
endmodule

module Full_Adder (
  input  Cin,
  input  a,
  input  b,
  output out_4,
  output out_5
);

  wire and_1_out, and_2_out, and_3_out, xor_1_out;

  xor xor_1 (xor_1_out, a, b);
  and and_1 (and_1_out, Cin, a);
  and and_2 (and_2_out, a, b);
  and and_3 (and_3_out, Cin, b);
  xor xor_2 (out_4, xor_1_out, Cin);
  and and_4 (out_5, and_1_out, and_2_out, and_3_out);
endmodule

module Cpl_2 (
  input  [7:0] in_1,
  output C,
  output [7:0] out_3
);

  wire half_adder_1_c, half_adder_2_c, half_adder_3_c, half_adder_4_c, half_adder_5_c, half_adder_6_c,
       half_adder_8_c;
  wire [7:0] not_1_out;

  assign not_1_out = ~in_1;  // NOT_Gate not_1, 8 bits wide
  Half_Adder half_adder_1 (.S(out_3[0]), .C(half_adder_1_c), .a(1'b1), .b(not_1_out[0]));
  Half_Adder half_adder_2 (.S(out_3[2]), .C(half_adder_2_c), .a(not_1_out[2]), .b(half_adder_3_c));
  Half_Adder half_adder_3 (.S(out_3[1]), .C(half_adder_3_c), .a(not_1_out[1]), .b(half_adder_1_c));
  Half_Adder half_adder_4 (.S(out_3[4]), .C(half_adder_4_c), .a(not_1_out[4]), .b(half_adder_5_c));
  Half_Adder half_adder_5 (.S(out_3[3]), .C(half_adder_5_c), .a(not_1_out[3]), .b(half_adder_2_c));
  Half_Adder half_adder_6 (.S(out_3[5]), .C(half_adder_6_c), .a(not_1_out[5]), .b(half_adder_4_c));
  Half_Adder half_adder_7 (.S(out_3[7]), .C(C), .a(not_1_out[7]), .b(half_adder_8_c));
  Half_Adder half_adder_8 (.S(out_3[6]), .C(half_adder_8_c), .a(not_1_out[6]), .b(half_adder_6_c));
endmodule

module Overflow (
);

  Adder_4_bits adder_4_bits_1 ();  // open: in_3, in_6, in_9, in_12, in_13, in_1, in_2, in_4, in_5, in_7, in_8, in_10, in_11
endmodule

module Adder_4_bits (
  input  in_1,
  input  in_2,
  input  in_3,
  input  in_4,
  input  in_5,
  input  in_6,
  input  in_7,
  input  in_8,
  input  in_9,
  input  in_10,
  input  in_11,
  input  in_12,
  input  in_13
);

  wire full_adder_1_out_5, full_adder_2_out_5, half_adder_1_c;

  Half_Adder half_adder_1 (.S(in_3), .C(half_adder_1_c), .a(in_1), .b(in_2));
  Full_Adder full_adder_1 (.Cin(half_adder_1_c), .a(in_4), .b(in_5), .out_4(in_6), .out_5(full_adder_1_out_5));
  Full_Adder full_adder_2 (.Cin(full_adder_1_out_5), .a(in_7), .b(in_8), .out_4(in_9), .out_5(full_adder_2_out_5));
  Full_Adder full_adder_3 (.Cin(full_adder_2_out_5), .a(in_10), .b(in_11), .out_4(in_12), .out_5(in_13));
endmodule

module and_8_bit (
  input  [7:0] in_1,
  input  [7:0] in_2,
  output [7:0] out_3
);

  assign out_3 = in_1 & in_2;  // AND_Gate and_1, 8 bits wide
endmodule

module not_8_bit (
  input  [7:0] in_1,
  output [7:0] out_2
);

  assign out_2 = ~in_1;  // NOT_Gate not_1, 8 bits wide
endmodule

module or_8_bit (
  input  [7:0] in_1,
  input  [7:0] in_2,
  output [7:0] out_3
);

  assign out_3 = in_1 | in_2;  // OR_Gate or_1, 8 bits wide
endmodule

module ex_or_8_bit (
  input  [7:0] in_1,
  input  [7:0] in_2,
  output [7:0] out_3
);

  assign out_3 = in_1 ^ in_2;  // XOR_Gate xor_1, 8 bits wide
endmodule
